// Logisim project bc.circ as structural Verilog: 6 circuits, main circuit b_log
module b_log (
  input  CLR,
  input  CLK
);

  wire n74194_1_qa, n74194_1_qb, n74194_1_qc, n74194_1_qd, nand_1_out, not_1_out;

  not not_1 (not_1_out, CLR);
  _74194 u_74194_1 (
    .S0(1'b0), .S1(CLR), .SR(1'b0), .CLK(CLK), .CLR(not_1_out), .SL(nand_1_out), .A(1'b0), .B(1'b0),
    .C(1'b0), .D(1'b0), .QA(n74194_1_qa), .QB(n74194_1_qb), .QC(n74194_1_qc), .QD(n74194_1_qd));
  LED led_1 (.in(n74194_1_qa));
  nand nand_1 (nand_1_out, n74194_1_qd, n74194_1_qc, n74194_1_qb);
  LED led_2 (.in(n74194_1_qd));
  LED led_3 (.in(n74194_1_qc));
  LED led_4 (.in(n74194_1_qb));

  // Notes on the sheet:
  //   S0
  //   Sr
  //   d
  //   c
  //   b
  //   S1
  //   a
  //   Schemat Logiczny Układu B
  //   Sl
  //   Qd
  //   Qc
  //   Qb
  //   Qa
endmodule

module c_log (
  input  CLR,
  input  S1,
  input  Clk
);

  wire n74194_1_qa, n74194_1_qb, n74194_1_qc, n74194_1_qd, not_1_out, not_2_out;

  not not_1 (not_1_out, CLR);
  _74194 u_74194_1 (
    .S0(1'b0), .S1(S1), .SR(1'b0), .CLK(Clk), .CLR(not_1_out), .SL(not_2_out), .A(1'b0), .B(1'b0), .C(1'b0),
    .D(1'b0), .QA(n74194_1_qa), .QB(n74194_1_qb), .QC(n74194_1_qc), .QD(n74194_1_qd));
  not not_2 (not_2_out, n74194_1_qa);
  LED led_1 (.in(n74194_1_qc));
  LED led_2 (.in(n74194_1_qb));
  LED led_3 (.in(n74194_1_qa));
  LED led_4 (.in(n74194_1_qd));

  // Notes on the sheet:
  //   b
  //   S0
  //   Sr
  //   d
  //   c
  //   a
  //   Sl
  //   Układ c
  //   Qb
  //   Qa
  //   Qd
  //   Qc
endmodule

module a_log (
  input  CLR,
  input  CLK,
  input  S1
);

  wire n74194_1_qa, n74194_1_qb, n74194_1_qc, n74194_1_qd, not_1_out;

  not not_1 (not_1_out, CLR);
  _74194 u_74194_1 (
    .S0(S1), .S1(CLR), .SR(1'b0), .CLK(CLK), .CLR(not_1_out), .SL(n74194_1_qa), .A(1'b0), .B(1'b0), .C(1'b0),
    .D(CLR), .QA(n74194_1_qa), .QB(n74194_1_qb), .QC(n74194_1_qc), .QD(n74194_1_qd));
  LED led_1 (.in(n74194_1_qb));
  LED led_2 (.in(n74194_1_qa));
  LED led_3 (.in(n74194_1_qd));
  LED led_4 (.in(n74194_1_qc));

  // Notes on the sheet:
  //   S0
  //   Schemat logiczny układu A
  //   Sr
  //   d
  //   c
  //   a
  //   Sl
  //   Qa
  //   Qd
  //   Qc
  //   Qb
endmodule

module a_pod (
  input  CLR,
  input  S1
);

  wire clock_1_out, n7404_1_p2, n7404_1_p3, n74194_1_qa, n74194_1_qb, n74194_1_qc;

  // _7404 7404_1: pin names not known; wires that end beside it: CLR, n7404_1_p2, n7404_1_p3
  Clock clock_1 (.out(clock_1_out));
  _74194 u_74194_1 (
    .S0(S1), .S1(CLR), .SR(1'b0), .CLK(clock_1_out), .CLR(n7404_1_p2), .SL(n74194_1_qa), .A(1'b0), .B(1'b0),
    .C(1'b0), .D(CLR), .QA(n74194_1_qa), .QB(n74194_1_qb), .QC(n74194_1_qc), .QD(n7404_1_p3));
  LED led_1 (.in(n74194_1_qb));
  LED led_2 (.in(n74194_1_qa));
  LED led_3 (.in(n7404_1_p3));
  LED led_4 (.in(n74194_1_qc));

  // Notes on the sheet:
  //   S0
  //   Sr
  //   d
  //   c
  //   b
  //   a
  //   Sl
  //   Układ A_pod
  //   CLK
  //   Qa
  //   Qd
  //   Qc
  //   Qb
endmodule

module b_pod (
  input  in_1
);

  wire clock_1_out, n7404_1_p2, n7410_1_p1, n74194_1_qa, n74194_1_qb, n74194_1_qc, n74194_1_qd;

  // _7404 7404_1: pin names not known; wires that end beside it: in_1, n7404_1_p2
  _74194 u_74194_1 (
    .S0(1'b0), .S1(in_1), .SR(1'b0), .CLK(clock_1_out), .CLR(n7404_1_p2), .SL(n7410_1_p1), .A(1'b0),
    .B(1'b0), .C(1'b0), .D(1'b0), .QA(n74194_1_qa), .QB(n74194_1_qb), .QC(n74194_1_qc), .QD(n74194_1_qd));
  LED led_1 (.in(n74194_1_qa));
  // _7410 7410_1: pin names not known; wires that end beside it: n7410_1_p1, n74194_1_qb, n74194_1_qd, n74194_1_qc
  Clock clock_1 (.out(clock_1_out));
  LED led_2 (.in(n74194_1_qd));
  LED led_3 (.in(n74194_1_qc));
  LED led_4 (.in(n74194_1_qb));

  // Notes on the sheet:
  //   S0
  //   Sr
  //   d
  //   c
  //   b
  //   S1
  //   a
  //   CLR
  //   Sl
  //   b_pod
  //   CLK
  //   Qd
  //   Qc
  //   Qb
  //   Qa
endmodule

module c_pod (
  input  CLR,
  input  S1
);

  wire clock_1_out, n7404_1_p2, n7404_1_p3, n7404_1_p4, n74194_1_qb, n74194_1_qc, n74194_1_qd;

  // _7404 7404_1: pin names not known; wires that end beside it: CLR, n7404_1_p2, n7404_1_p3, n7404_1_p4
  _74194 u_74194_1 (
    .S0(1'b0), .S1(S1), .SR(1'b0), .CLK(clock_1_out), .CLR(n7404_1_p2), .SL(n7404_1_p4), .A(1'b0), .B(1'b0),
    .C(1'b0), .D(1'b0), .QA(n7404_1_p3), .QB(n74194_1_qb), .QC(n74194_1_qc), .QD(n74194_1_qd));
  Clock clock_1 (.out(clock_1_out));
  LED led_1 (.in(n74194_1_qc));
  LED led_2 (.in(n74194_1_qb));
  LED led_3 (.in(n7404_1_p3));
  LED led_4 (.in(n74194_1_qd));

  // Notes on the sheet:
  //   b
  //   C_pod
  //   S0
  //   Sr
  //   d
  //   c
  //   a
  //   Sl
  //   Clk
  //   Qb
  //   Qa
  //   Qd
  //   Qc
endmodule
