// Logisim project Samulski_Suchanek.circ as structural Verilog: 12 circuits, main circuit A_MUX_Logiczny
module A_MUX_Logiczny (
  input  STROBE,
  input  b,
  input  c,
  input  d,
  input  a
);

  wire n74151_1_p2, n74151_1_p5;

  LED led_1 (.in(n74151_1_p5));
  // _74151 74151_1: pin names not known; wires that end beside it: 1'b0, n74151_1_p2, 1'b0, 1'b1, n74151_1_p5, STROBE, 1'b0, 1'b1, 1'b1, 1'b0, 1'b0, 1'b0, d, c, b
  not not_1 (n74151_1_p2, a);

  // Notes on the sheet:
  //   O1
  //   A MUX_log
endmodule

module A_NAND_log (
  input  a,
  input  b,
  input  c,
  input  d
);

  wire nand_1_out, nand_2_out, nand_3_out, not_1_out, not_2_out, not_3_out, not_4_out;

  not not_1 (not_1_out, a);
  not not_2 (not_2_out, b);
  not not_3 (not_3_out, c);
  not not_4 (not_4_out, d);
  nand nand_1 (nand_1_out, not_3_out, not_4_out);
  nand nand_2 (nand_2_out, not_1_out, not_2_out, not_4_out);
  LED led_1 (.in(nand_3_out));
  nand nand_3 (nand_3_out, nand_1_out, nand_2_out);

  // Notes on the sheet:
  //   A_NAND
  //   O1
endmodule

module B_MUX_log (
  input  Strobe,
  input  a,
  input  b,
  input  c
);

  wire n74151_1_p5;

  LED led_1 (.in(n74151_1_p5));
  // _74151 74151_1: pin names not known; wires that end beside it: 1'b1, 1'b1, 1'b0, 1'b1, n74151_1_p5, Strobe, 1'b0, 1'b1, 1'b1, 1'b1, 1'b0, 1'b1, c, b, a

  // Notes on the sheet:
  //   B_MUX_log
  //   O1
endmodule

module B_NAND_LOg (
  input  a,
  input  b,
  input  c
);

  wire nand_1_out, nand_2_out, nand_3_out, nand_4_out, nand_5_out, nand_6_out, nand_7_out;

  nand nand_1 (nand_1_out, a, a);
  nand nand_2 (nand_2_out, b, b);
  nand nand_3 (nand_3_out, c, c);
  nand nand_4 (nand_4_out, nand_2_out, nand_3_out);
  nand nand_5 (nand_5_out, a, c);
  nand nand_6 (nand_6_out, nand_1_out, b);
  nand nand_7 (nand_7_out, nand_4_out, nand_5_out, nand_6_out);
  LED led_1 (.in(nand_7_out));

  // Notes on the sheet:
  //   B_NAND
  //   O1
endmodule

module \A_Mux_Podłączenie  (
  input  STROBE,
  input  b,
  input  c,
  input  d,
  input  a
);

  wire n74151_1_p2, n74151_1_p5;

  LED led_1 (.in(n74151_1_p5));
  // _74151 74151_1: pin names not known; wires that end beside it: 1'b0, n74151_1_p2, 1'b0, 1'b1, n74151_1_p5, STROBE, 1'b0, 1'b1, 1'b1, 1'b0, 1'b0, 1'b0, d, c, b
  // _7404 7404_1: pin names not known; wires that end beside it: n74151_1_p2, a

  // Notes on the sheet:
  //   O1
  //   A_MUX_POD
endmodule

module A_NAND_POD (
  input  a,
  input  b,
  input  c,
  input  d
);

  wire n7400_1_p3, n7400_1_p4, n7404_1_p2, n7404_1_p4, n7404_1_p7, n7404_1_p8, n7410_1_p3;

  // _7404 7404_1: pin names not known; wires that end beside it: c, n7404_1_p2, b, n7404_1_p4, d, a, n7404_1_p7, n7404_1_p8
  // _7400 7400_1: pin names not known; wires that end beside it: n7404_1_p2, n7404_1_p7, n7400_1_p3, n7400_1_p4, n7400_1_p3
  // _7410 7410_1: pin names not known; wires that end beside it: n7404_1_p4, n7404_1_p8, n7410_1_p3, n7404_1_p7, n7400_1_p4, n7410_1_p3
  LED led_1 (.in(n7410_1_p3));

  // Notes on the sheet:
  //   A_NAND_Pod
  //   O1
endmodule

module B_NAND_POD (
  input  a,
  input  b,
  input  c
);

  wire n7400_1_p3, n7400_1_p6, n7400_1_p9, n7404_1_p2, n7404_1_p4, n7404_1_p6, n7410_1_p4;

  // _7404 7404_1: pin names not known; wires that end beside it: a, n7404_1_p2, b, n7404_1_p4, c, n7404_1_p6
  // _7400 7400_1: pin names not known; wires that end beside it: n7404_1_p6, n7404_1_p4, n7400_1_p3, a, c, n7400_1_p6, b, n7404_1_p2, n7400_1_p9
  // _7410 7410_1: pin names not known; wires that end beside it: n7400_1_p9, n7400_1_p6, n7400_1_p3, n7410_1_p4
  LED led_1 (.in(n7410_1_p4));

  // Notes on the sheet:
  //   B_NAND_Pod
  //   O1
endmodule

module B_MUX_POD (
  input  Strobe,
  input  a,
  input  b,
  input  c
);

  wire n74151_1_p5;

  LED led_1 (.in(n74151_1_p5));
  // _74151 74151_1: pin names not known; wires that end beside it: 1'b1, 1'b1, 1'b0, 1'b1, n74151_1_p5, Strobe, 1'b0, 1'b1, 1'b1, 1'b1, 1'b0, 1'b1, c, b, a

  // Notes on the sheet:
  //   B_MUX_Pod
  //   O1
endmodule

module A_Razem_Log (
  input  a,
  input  b,
  input  c,
  input  d
);

  wire n74151_1_p2, n74151_1_p5, nand_1_out, nand_2_out, nand_3_out, nand_4_out, nand_5_out, nand_6_out,
       nand_7_out;

  // _74151 74151_1: pin names not known; wires that end beside it: 1'b0, n74151_1_p2, 1'b0, 1'b1, n74151_1_p5, 1'b0, 1'b0, 1'b1, 1'b1, 1'b0, 1'b0, 1'b0, d, c, b
  not not_1 (n74151_1_p2, a);
  nand nand_1 (nand_1_out, a, a);
  nand nand_2 (nand_2_out, b, b);
  nand nand_3 (nand_3_out, c, c);
  nand nand_4 (nand_4_out, d, d);
  nand nand_5 (nand_5_out, nand_3_out, nand_4_out);
  nand nand_6 (nand_6_out, nand_1_out, nand_2_out, nand_4_out);
  nand nand_7 (nand_7_out, nand_5_out, nand_6_out);
  LED led_1 (.in(n74151_1_p5));
  LED led_2 (.in(nand_7_out));

  // Notes on the sheet:
  //   A_Razem_Log
  //   O1
  //   O2
endmodule

module A_Razem_Pod (
  input  STROBE,
  input  b,
  input  c,
  input  d,
  input  a
);

  wire n7400_1_p3, n7400_1_p4, n7404_2_p2, n7404_2_p4, n7404_2_p7, n7404_2_p8, n7410_1_p3, n74151_1_p2,
       n74151_1_p5;

  LED led_1 (.in(n74151_1_p5));
  // _74151 74151_1: pin names not known; wires that end beside it: 1'b0, n74151_1_p2, 1'b0, 1'b1, n74151_1_p5, STROBE, 1'b0, 1'b1, 1'b1, 1'b0, 1'b0, 1'b0, d, c, b
  // _7404 7404_1: pin names not known; wires that end beside it: n74151_1_p2, a
  // _7404 7404_2: pin names not known; wires that end beside it: c, n7404_2_p2, b, n7404_2_p4, d, a, n7404_2_p7, n7404_2_p8
  // _7400 7400_1: pin names not known; wires that end beside it: n7404_2_p2, n7404_2_p7, n7400_1_p3, n7400_1_p4, n7400_1_p3
  // _7410 7410_1: pin names not known; wires that end beside it: n7404_2_p4, n7404_2_p8, n7410_1_p3, n7404_2_p7, n7400_1_p4, n7410_1_p3
  LED led_2 (.in(n7410_1_p3));

  // Notes on the sheet:
  //   O1
  //   A_Razem_Pod
  //   O1
endmodule

module B_Razem_log (
  input  a,
  input  b,
  input  c
);

  wire n74151_1_p5, nand_1_out, nand_2_out, nand_3_out, nand_4_out, nand_5_out, nand_6_out, nand_7_out;

  // _74151 74151_1: pin names not known; wires that end beside it: 1'b1, 1'b1, 1'b0, 1'b1, n74151_1_p5, 1'b0, 1'b0, 1'b1, 1'b1, 1'b1, 1'b0, 1'b1, c, b, a
  nand nand_1 (nand_1_out, a, a);
  nand nand_2 (nand_2_out, b, b);
  nand nand_3 (nand_3_out, c, c);
  nand nand_4 (nand_4_out, nand_2_out, nand_3_out);
  nand nand_5 (nand_5_out, a, c);
  nand nand_6 (nand_6_out, nand_1_out, b);
  LED led_1 (.in(n74151_1_p5));
  nand nand_7 (nand_7_out, nand_4_out, nand_5_out, nand_6_out);
  LED led_2 (.in(nand_7_out));

  // Notes on the sheet:
  //   B_razem_log
  //   O1
  //   O2
endmodule

module B_Razem_Pod (
  input  Strobe,
  input  a,
  input  b,
  input  c
);

  wire n7400_1_p3, n7400_1_p6, n7400_1_p9, n7404_1_p2, n7404_1_p4, n7404_1_p6, n7410_1_p4, n74151_1_p5;

  LED led_1 (.in(n74151_1_p5));
  // _74151 74151_1: pin names not known; wires that end beside it: 1'b1, 1'b1, 1'b0, 1'b1, n74151_1_p5, Strobe, 1'b0, 1'b1, 1'b1, 1'b1, 1'b0, 1'b1, c, b, a
  // _7404 7404_1: pin names not known; wires that end beside it: a, n7404_1_p2, b, n7404_1_p4, c, n7404_1_p6
  // _7400 7400_1: pin names not known; wires that end beside it: n7404_1_p6, n7404_1_p4, n7400_1_p3, a, c, n7400_1_p6, b, n7404_1_p2, n7400_1_p9
  // _7410 7410_1: pin names not known; wires that end beside it: n7400_1_p9, n7400_1_p6, n7400_1_p3, n7410_1_p4
  LED led_2 (.in(n7410_1_p4));

  // Notes on the sheet:
  //   O1
  //   B_razem_Pod
  //   O2
endmodule
