// Logisim project Samulski_Suchanek_lab5.circ as structural Verilog: 3 circuits, main circuit MOORE
module MOORE (
  input  X,
  input  CLK
);

  wire d_ff_1_q, d_ff_1_qn, d_ff_2_q, d_ff_2_qn, nand_1_out, nand_2_out, nand_3_out, nor_1_out, nor_2_out,
       not_1_out;

  not not_1 (not_1_out, X);
  nand nand_1 (nand_1_out, d_ff_1_q, not_1_out);
  nand nand_2 (nand_2_out, X, d_ff_1_qn);
  nand nand_3 (nand_3_out, nand_1_out, nand_2_out);
  D_Flip_Flop d_ff_1 (.clk(CLK), .D(nand_3_out), .Q(d_ff_1_q), .Qn(d_ff_1_qn), .preset(1'b0), .en(1'b1), .reset(1'b0));
  D_Flip_Flop d_ff_2 (.clk(CLK), .D(d_ff_1_q), .Q(d_ff_2_q), .Qn(d_ff_2_qn), .preset(1'b0), .en(1'b1), .reset(1'b0));
  nor nor_1 (nor_1_out, d_ff_1_qn, d_ff_2_q);
  nor nor_2 (nor_2_out, d_ff_1_q, d_ff_2_qn);
  LED led_1 (.in(nor_1_out));
  LED led_2 (.in(nor_2_out));

  // Notes on the sheet:
  //   Z1
  //   Z2
endmodule

module MEALY (
  input  X,
  input  Clk
);

  wire j_k_ff_1_q, j_k_ff_1_qn, nor_1_out, nor_2_out, not_1_out;

  not not_1 (not_1_out, X);
  J_K_Flip_Flop j_k_ff_1 (
    .J(X), .clk(Clk), .K(X), .Q(j_k_ff_1_q), .Qn(j_k_ff_1_qn), .preset(1'b0), .en(1'b1), .reset(1'b0));
  nor nor_1 (nor_1_out, not_1_out, j_k_ff_1_qn);
  nor nor_2 (nor_2_out, not_1_out, j_k_ff_1_q);
  LED led_1 (.in(nor_1_out));
  LED led_2 (.in(nor_2_out));

  // Notes on the sheet:
  //   Z1
  //   Z2
endmodule

module Razem (
  input  X,
  input  CLK
);

  wire d_ff_1_q, d_ff_1_qn, d_ff_2_q, d_ff_2_qn, j_k_ff_1_q, j_k_ff_1_qn, nand_1_out, nand_2_out, nand_3_out,
       nor_1_out, nor_2_out, nor_3_out, nor_4_out, not_1_out, not_2_out;

  not not_1 (not_1_out, X);
  not not_2 (not_2_out, X);
  J_K_Flip_Flop j_k_ff_1 (
    .J(X), .clk(CLK), .K(X), .Q(j_k_ff_1_q), .Qn(j_k_ff_1_qn), .preset(1'b0), .en(1'b1), .reset(1'b0));
  nand nand_1 (nand_1_out, d_ff_1_q, not_2_out);
  nand nand_2 (nand_2_out, X, d_ff_1_qn);
  nand nand_3 (nand_3_out, nand_1_out, nand_2_out);
  D_Flip_Flop d_ff_1 (.clk(CLK), .D(nand_3_out), .Q(d_ff_1_q), .Qn(d_ff_1_qn), .preset(1'b0), .en(1'b1), .reset(1'b0));
  D_Flip_Flop d_ff_2 (.clk(CLK), .D(d_ff_1_q), .Q(d_ff_2_q), .Qn(d_ff_2_qn));  // open: preset, en, reset
  nor nor_1 (nor_1_out, not_1_out, j_k_ff_1_qn);
  nor nor_2 (nor_2_out, not_1_out, j_k_ff_1_q);
  nor nor_3 (nor_3_out, d_ff_1_qn, d_ff_2_q);
  nor nor_4 (nor_4_out, d_ff_1_q, d_ff_2_qn);
  LED led_1 (.in(nor_3_out));
  LED led_2 (.in(nor_4_out));
  LED led_3 (.in(nor_1_out));
  LED led_4 (.in(nor_2_out));

  // Notes on the sheet:
  //   Z1
  //   Z2
  //   Z3
  //   Z4
endmodule
